# Fritzing sketch wireless_base_design_5v (saved by Fritzing 0.9.3b)
perfboards: 1

parts:
  IC1 = MICROCONTROLLER [package=dil28-3]
  J2 = female pin header, 4 pins [form="♀ (female)"]
  J3 = female pin header, 4 pins [form="♀ (female)"]
  R1 = Resistor [tolerance=±5% resistance=120 package=THT]
  LED1 = LED - 3mm [color="Yellow (595nm)" package="3 mm [THT]"]
  R2 = Resistor [tolerance=±5% resistance=120 power=0pW package=THT]
  LED2 = LED - 3mm [color="Red (633nm)" package="3 mm [THT]"]
  IC2 = Voltage Regulator [package=to-92]

nets:
  N1: IC1.VCC, IC1.AVCC, IC2.IN
  N2: IC1.GND, IC1.AGND, LED1.cathode, LED2.cathode
  N3: IC1.PD5(T1), R2.Pin_1
  N4: IC1.PD6(AIN0), R1.Pin_1
  N5: IC1.PB1(OC1A), J2.pin2
  N6: IC1.PB2(SS_OC1B), J3.pin2
  N7: IC1.PB3(MOSI_OC2), J3.pin3
  N8: IC1.PB4(MISO), J2.pin4
  N9: IC1.PB5(SCK), J2.pin3
  N10: J2.pin1, IC2.GND
  N11: J3.pin1, IC2.OUT
  N12: R1.Pin_0, LED1.anode
  N13: R2.Pin_0, LED2.anode
